# Fritzing sketch schaltplan_garage (saved by Fritzing 0.9.4)
breadboards: 1

parts:
  Part1 = Arduino MKR1000
  Part2 = Adafruit TSL2561 [part_number="Adafruit #439"]
  LED1 = LEDs [package=led10mm]
  hc-sr1 = hc-sr04
  hc-sr2 = hc-sr04
  hc-sr3 = hc-sr04
  Part3 = songle relay
  Part4 = songle relay
  M1 = DC Motor

nets:
  N1: Part1.D0, Part3.COMMON
  N2: Part1.D1, Part4.COMMON
  N3: Part1.D2_PWM, hc-sr1.Echo
  N4: Part1.D3_PWM, hc-sr2.Echo
  N5: Part1.D4_PWM, hc-sr3.Echo
  N6: Part1.D5_PWM, hc-sr1.Trig
  N7: Part1.D11_SDA, Part2.SDA
  N8: Part1.D12_SCL, Part2.SCL
  GND: Part1.GND, Part2.GND, LED1.A, hc-sr1.GND, hc-sr2.GND, hc-sr3.GND, Part3.GND, Part4.GND
  VCC: Part1.VCC, Part2.VIN, LED1.C, hc-sr1.VCC, hc-sr2.VCC, hc-sr3.VCC, Part3.VCC, Part4.VCC
  N9: Part3.NO, M1.pin_2
  N10: Part4.NO, M1.pin_1

notes:
  Steckdose

custom parts:
  Arduino MKR1000: MKR1000 is a powerful board that combines the functionality of the Zero and the Wi-Fi Shield. It is the ideal solution for makers wanting to design IoT projects with minimal previous experience in networking
  Adafruit TSL2561: The TSL2561 luminosity sensor is an advanced digital light sensor, ideal for use in a wide range of light situations. Compared to low cost CdS cells, this sensor is more precise, allowing for exact lux calculations and can be configured for different gain/timing ranges to detect light ranges from up to 0.1 - 40,000+ Lux on the fly. The best part of this sensor is that it contains both infrared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
