# Fritzing sketch schaltung_auto (saved by Fritzing 0.9.4)

parts:
  Part1 = Bluetooth HM-10
  M1 = Arduino Uno WIFI REV2

nets:
  N1: Part1.RXD, M1.D3_PWM
  N2: Part1.TXD, M1.D2
  GND: Part1.GND, M1.GND
  VCC: Part1.VCC, M1.3V3

custom parts:
  Arduino Uno WIFI REV2: The Arduino Uno WIFI REV2 is a microcontroller board based on the ATmega 4809. It has 14 digital input/output pins (of which 5 can be used as PWM outputs), 6 analog inputs, a 16 MHz ceramic resonator, a USB connection, a power jack, an ICSP header, and a reset button. It also has a WIFI controller with a secure ECC608 crypto unit and an internal IMU. It contains everything needed to support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
